# Fritzing sketch nano - ulrasensor distance (saved by Fritzing 0.9.2b)
breadboards: 1

parts:
  Part1 = Arduino Nano (Rev3.0) (ICSP)
  Part2 = SRF05 Ultrasonic Rangefinder
  LCD1 = LCD screen
  LCM1602_IIC1 = LCM1602 IIC [part_number="LCM1602 IIC" chip_label="LCM1602 IIC" package="DIP (Dual Inline) [THT]"]

nets:
  GND: Part1.GND, Part2.GND, LCM1602_IIC1.GND
  N1: Part1.D7, Part2.Echo
  N2: Part1.D8, Part2.Trig
  VCC: Part1.5V, Part2.VCC, LCM1602_IIC1.VCC
  N3: Part1.A5, LCM1602_IIC1.SCL
  N4: Part1.A4, LCM1602_IIC1.SDA
  VSS: LCD1.VSS, LCM1602_IIC1.VSS
  VDD: LCD1.VDD, LCM1602_IIC1.VDD
  N5: LCD1.V0, LCM1602_IIC1.V0
  N6: LCD1.RS, LCM1602_IIC1.RS
  N7: LCD1.R/W, LCM1602_IIC1.RW
  N8: LCD1.E, LCM1602_IIC1.E
  N9: LCD1.DB0, LCM1602_IIC1.D0
  N10: LCD1.DB1, LCM1602_IIC1.D1
  N11: LCD1.DB2, LCM1602_IIC1.D2
  N12: LCD1.DB3, LCM1602_IIC1.D3
  N13: LCD1.DB4, LCM1602_IIC1.D4
  N14: LCD1.DB5, LCM1602_IIC1.D5
  N15: LCD1.DB6, LCM1602_IIC1.D6
  N16: LCD1.DB7, LCM1602_IIC1.D7
  N17: LCD1.LED+, LCM1602_IIC1.A
  N18: LCD1.LED-, LCM1602_IIC1.K

custom parts:
  LCM1602 IIC: I2C-Module to use a 1602 or 2004 LCD on with the wire.h libory Serial LCD Modul

// code stored in the sketch: nano - ulrasensor distance.ino


#include <dht.h>
#include <Wire.h> 
#include <LiquidCrystal_I2C.h>

LiquidCrystal_I2C lcd(0x3F,20,4);


const int pingPin = 7; // Trigger Pin of Ultrasonic Sensor
const int echoPin = 6; // Echo Pin of Ultrasonic Sensor

void setup() {
   Serial.begin(9600); // Starting Serial Terminal
   lcd.init();
       // Print a message to the LCD.
    lcd.backlight();
}

void loop() {


   long duration, inches, cm;
   pinMode(pingPin, OUTPUT);
   digitalWrite(pingPin, LOW);
   delayMicroseconds(2);
   digitalWrite(pingPin, HIGH);
   delayMicroseconds(10);
   digitalWrite(pingPin, LOW);
   pinMode(echoPin, INPUT);
   duration = pulseIn(echoPin, HIGH);
   inches = microsecondsToInches(duration);
   cm = microsecondsToCentimeters(duration);
   lcd.setCursor(0,0); 
   lcd.print("Distance: ");
   lcd.print(cm);
   lcd.print(" cm");
   lcd.print("  ");
   lcd.setCursor(0,1);
   lcd.print("       ");
   lcd.print(inches);
   lcd.print(" inches");
   lcd.print("  ");
  delay(100);
   
   
   //Serial.print(inches);
  // Serial.print("in, ");
  // Serial.print(cm);
   //Serial.print("cm");
  // Serial.println();
  // delay(100);
}

long microsecondsToInches(long microseconds) {
   return microseconds / 74 / 2;
}

long microsecondsToCentimeters(long microseconds) {
   return microseconds / 29 / 2;
}
