# Fritzing sketch temp sensor lcd (saved by Fritzing 0.9.2b)
breadboards: 1

parts:
  Part1 = Arduino Uno (Rev3)
  LCD1 = LCD screen
  LCM1602_IIC2 = LCM1602 IIC [part_number="LCM1602 IIC" chip_label="LCM1602 IIC" package="DIP (Dual Inline) [THT]"]
  DHT1 = DHT11 Humitidy and Temperature Sensor
  R1 = Resistor [tolerance=±5% resistance=10k package="2512 [SMD]"]

nets:
  N1: Part1.A4/SDA, LCM1602_IIC2.SDA
  N2: Part1.A5/SCL, LCM1602_IIC2.SCL
  N3: Part1.D7, DHT1.DATA, R1.Pin_1
  5V: Part1.5V, LCM1602_IIC2.VCC
  GND: Part1.GND, LCM1602_IIC2.GND, DHT1.GND
  VSS: LCD1.VSS, LCM1602_IIC2.VSS
  VDD: LCD1.VDD, LCM1602_IIC2.VDD
  N4: LCD1.V0, LCM1602_IIC2.V0
  N5: LCD1.RS, LCM1602_IIC2.RS
  N6: LCD1.R/W, LCM1602_IIC2.RW
  N7: LCD1.E, LCM1602_IIC2.E
  N8: LCD1.DB0, LCM1602_IIC2.D0
  N9: LCD1.DB1, LCM1602_IIC2.D1
  N10: LCD1.DB2, LCM1602_IIC2.D2
  N11: LCD1.DB3, LCM1602_IIC2.D3
  N12: LCD1.DB4, LCM1602_IIC2.D4
  N13: LCD1.DB5, LCM1602_IIC2.D5
  N14: LCD1.DB6, LCM1602_IIC2.D6
  N15: LCD1.DB7, LCM1602_IIC2.D7
  N16: LCD1.LED+, LCM1602_IIC2.A
  N17: LCD1.LED-, LCM1602_IIC2.K
  N18: DHT1.VDD, R1.Pin_0

custom parts:
  LCM1602 IIC: I2C-Module to use a 1602 or 2004 LCD on with the wire.h libory Serial LCD Modul
  DHT11 Humitidy and Temperature Sensor: DHT11 Humidity and Temperature Sensor

// code stored in the sketch: temp sensor lcd.ino
//YWROBOT
//Compatible with the Arduino IDE 1.0
//Library version:1.1
#include <dht.h>
#include <Wire.h> 
#include <LiquidCrystal_I2C.h>

LiquidCrystal_I2C lcd(0x3F,20,4);  // set the LCD address to 0x3F for a 16 chars and 2 line display

dht DHT;
#define DHT11_PIN 7

void setup()
{
  lcd.init();                      // initialize the lcd 
  lcd.init();
  // Print a message to the LCD.
  lcd.backlight();
  lcd.setCursor(3,0);
  lcd.print("Hello, world!");
  lcd.setCursor(2,1);
  lcd.print("Ywrobot Arduino!");
   lcd.setCursor(0,2);
  lcd.print("Arduino LCM IIC 2004");
   lcd.setCursor(2,3);
  lcd.print("Power By Ec-yuan!");
}


void loop()
{
  int chk = DHT.read11(DHT11_PIN);
  lcd.setCursor(0,0); 
  lcd.print("Temp: ");
  lcd.print(DHT.temperature);
  lcd.print((char)223);
  lcd.print("C");
  lcd.print("   ");
  lcd.setCursor(0,1);
  lcd.print("Humidity: ");
  lcd.print(DHT.humidity);
  lcd.print("%");
  delay(1200);
}
